# Fritzing sketch relay_control (saved by Fritzing 0.9.3b)

parts:
  4_channel_relay_module(5v) = Module 4 Relais 5V [package="Module 4 Relais 5V"]
  DHT11 = DHT11 module
  BreadBoard_power_supply = Breadboard Power Supply Board SMD
  LED = LED - 3mm [color="Red (633nm)" package="3 mm [THT]"]
  Node_mcu_v0_9 = ESP8266 NodeMCU LoLin module

nets:
  VCC: 4_channel_relay_module(5v).VCC, BreadBoard_power_supply.VCC, Node_mcu_v0_9.Vin
  GND: 4_channel_relay_module(5v).GND, DHT11.GND, BreadBoard_power_supply.GND, LED.cathode, Node_mcu_v0_9.GND
  N1: 4_channel_relay_module(5v).IN1, Node_mcu_v0_9.D0
  N2: 4_channel_relay_module(5v).IN2, Node_mcu_v0_9.D1
  N3: 4_channel_relay_module(5v).IN3, Node_mcu_v0_9.D2
  N4: 4_channel_relay_module(5v).IN4, Node_mcu_v0_9.D3
  VCC_2: DHT11.VCC, Node_mcu_v0_9.3V3
  N5: DHT11.DATA, Node_mcu_v0_9.D5
  N6: LED.anode, Node_mcu_v0_9.D6

custom parts:
  Module 4 Relais 5V: Module 4 Relais 5V 4x SPD-06VDC-SD-C
  DHT11 module: DHT11 black pcb module
  ESP8266 NodeMCU LoLin module: ESP8266 based NodeMCU
